# Fritzing sketch PN532-adapter-shield (saved by Fritzing 0.9.2b)
circuit board: 6.88566cm x 5.36311cm
breadboards: 1

parts:
  Board = Arduino Uno (Rev3)
  J1 = female pin header, 6 pins [form="♀ (female)"]
  IC1 = IC, DIP package, 16 pins [chip_label=4050]

nets:
  GND: Board.GND, J1.pin1, IC1.pin8
  N1: Board.D2, IC1.pin9
  N2: Board.D5_PWM, J1.pin4
  N3: Board.D6_PWM, IC1.pin11
  N4: Board.D7, IC1.pin14
  3.3V: Board.3V3, J1.pin6, IC1.pin1
  5V: Board.5V
  N5: J1.pin2, IC1.pin15
  N6: J1.pin3, IC1.pin12
  N7: J1.pin5, IC1.pin10

notes:
  CMoP
  DTN Strategy Blocks
  RFID adapter v0.1
