# Fritzing sketch strategy (saved by Fritzing 0.9.2b)
circuit board: 8.81229cm x 5.34313cm
breadboards: 1

parts:
  IC3 = IC, DIP package, 16 pins [chip_label=4050]
  J10 = female pin header, 6 pins [form="♀ (female)"]
  IC1 = IC, DIP package, 14 pins [chip_label=7408]
  Q1 = npn-Powertransistor [package="TO220 [THT]"]
  Q3 = npn-Powertransistor [package="TO220 [THT]"]
  Q4 = npn-Powertransistor [package="TO220 [THT]"]
  Q6 = npn-Powertransistor [package="TO220 [THT]"]
  Q8 = npn-Powertransistor [package="TO220 [THT]"]
  Q7 = npn-Powertransistor [package="TO220 [THT]"]
  Q5 = npn-Powertransistor [package="TO220 [THT]"]
  R3 = Resistor [tolerance=±5% resistance=1k package=THT]
  R7 = Resistor [tolerance=±5% resistance=1k package=THT]
  R4 = Resistor [tolerance=±5% resistance=1k package=THT]
  R8 = Resistor [tolerance=±5% resistance=1k package=THT]
  R1 = Resistor [tolerance=±5% resistance=1k package=THT]
  R5 = Resistor [tolerance=±5% resistance=1k package=THT]
  R2 = Resistor [tolerance=±5% resistance=1k package=THT]
  R6 = Resistor [tolerance=±5% resistance=1k package=THT]
  C1 = Tantalum Capacitor [capacitance=100nF package="100 mil [THT, tantalum]"]
  C2 = Tantalum Capacitor [capacitance=100nF package="100 mil [THT, tantalum]"]
  C3 = Tantalum Capacitor [capacitance=100nF package="100 mil [THT, tantalum]"]
  Q9 = NPN-Transistor [package="TO92 [THT]"]
  R9 = Resistor [tolerance=±5% resistance=10k package=THT]
  J9 = Power Jack [package=power_jack_pth]
  Part1 = Arduino Uno (Rev3)
  Q2 = npn-Powertransistor [package="TO220 [THT]"]
  IC2 = IC, DIP package, 14 pins [chip_label=7408]
  R10 = Resistor [tolerance=±5% resistance=1k package=THT]
  J1 = female pin header, 2 pins [form="♀ (female)"]
  J2 = female pin header, 2 pins [form="♀ (female)"]
  J3 = female pin header, 2 pins [form="♀ (female)"]
  J4 = female pin header, 2 pins [form="♀ (female)"]
  J5 = female pin header, 2 pins [form="♀ (female)"]
  J6 = female pin header, 2 pins [form="♀ (female)"]
  J7 = female pin header, 2 pins [form="♀ (female)"]
  J8 = female pin header, 2 pins [form="♀ (female)"]

nets:
  3.3V: IC3.pin1, J10.pin6, C3.+, Part1.3V3
  GND: IC3.pin8, J10.pin1, IC1.pin7, Q1.emitter, Q3.emitter, Q4.emitter, Q6.emitter, Q8.emitter, Q7.emitter, Q5.emitter, C1.-, C2.-, C3.-, Q9.E, J9.GND, Part1.GND, Q2.emitter, IC2.pin7
  N1: IC3.pin9, Part1.D2
  N2: IC3.pin10, J10.pin5
  N3: IC3.pin11, Part1.D8
  N4: IC3.pin12, J10.pin3
  N5: IC3.pin14, Part1.D9_PWM
  N6: IC3.pin15, J10.pin2
  N7: J10.pin4, Part1.D5_PWM
  N8: IC1.pin1, Part1.A0, IC2.pin1
  N9: IC1.pin2, IC1.pin5, IC1.pin10, IC1.pin13, Q9.C, R9.Pin_1
  N10: IC1.pin3, R1.Pin_1
  N11: IC1.pin4, Part1.A1, IC2.pin4
  N12: IC1.pin6, R2.Pin_1
  N13: IC1.pin8, R3.Pin_1
  N14: IC1.pin9, Part1.A2, IC2.pin9
  N15: IC1.pin11, R4.Pin_1
  N16: IC1.pin12, Part1.A3, IC2.pin12
  5V: IC1.pin14, C1.+, C2.+, R9.Pin_0, Part1.5V, IC2.pin14
  N17: Q1.base, R1.Pin_0
  N18: Q1.collector, J1.pin2
  N19: Q3.base, R3.Pin_0
  N20: Q3.collector, J3.pin2
  N21: Q4.base, R4.Pin_0
  N22: Q4.collector, J4.pin2
  N23: Q6.base, R6.Pin_0
  N24: Q6.collector, J6.pin2
  N25: Q8.base, R8.Pin_0
  N26: Q8.collector, J8.pin2
  N27: Q7.base, R7.Pin_0
  N28: Q7.collector, J7.pin2
  N29: Q5.base, R5.Pin_0
  N30: Q5.collector, J5.pin2
  N31: R7.Pin_1, IC2.pin8
  N32: R8.Pin_1, IC2.pin11
  N33: R5.Pin_1, IC2.pin3
  N34: R2.Pin_0, Q2.base
  N35: R6.Pin_1, IC2.pin6
  N36: Q9.B, R10.Pin_0
  12V: J9.PWR, Part1.VIN, J1.pin1, J2.pin1, J3.pin1, J4.pin1, J5.pin1, J6.pin1, J7.pin1, J8.pin1
  N37: Part1.A4/SDA, IC2.pin2, IC2.pin5, IC2.pin10, IC2.pin13, R10.Pin_1
  N38: Q2.collector, J2.pin2

notes:
  CMoP DTN Strategy
  Block Table
  RFID
  v0.3
  +3.3
  SCK
  MISO
  MOSI
  SS
  GND
  7408
  4050

custom parts:
  npn-Powertransistor: A npn transistor which can drive a higher load
